# Fritzing sketch MiniProject (saved by Fritzing 0.9.3b)
breadboards: 1

parts:
  Part1 = Arduino Uno (Rev3)
  LED1 = RGB LED (com. cathode, rgb) [package="5 mm [THT]"]
  S1 = Pushbutton [package="[THT]"]
  R1 = Resistor [tolerance=±5% resistance=330 package=THT]
  R2 = Resistor [tolerance=±5% resistance=330 package=THT]
  R3 = Resistor [tolerance=±5% resistance=330 package=THT]
  R4 = Resistor [tolerance=±5% resistance=330 package=THT]

nets:
  N1: Part1.D9_PWM, R2.Pin_0
  N2: Part1.D10_PWM/SS, R4.Pin_0
  N3: Part1.D11_PWM/MOSI, R3.Pin_0
  N4: Part1.D2, S1.Pin_1, S1.Pin_2, R1.Pin_0
  N5: Part1.5V, S1.Pin_3, S1.Pin_4
  N6: Part1.GND, LED1.common_cathode, R1.Pin_1, R4.Pin_1
  N7: LED1.red_anode, R2.Pin_1
  N8: LED1.blue_anode, R3.Pin_1
